// Logisim project exercise01.circ as structural Verilog: 2 circuits, main circuit main
module main (
  input  in_1
);
endmodule

module ex01 (
  input  A,
  input  B,
  output S
);

  wire NOR1_out, NOR2_out, NOR3_out;

  nor NOR1 (NOR1_out, A, A);
  nor NOR3 (NOR3_out, NOR1_out, NOR1_out);
  nor NOR2 (NOR2_out, B, B);
  nor NOR4 (S, NOR3_out, NOR2_out);
endmodule
