// Logisim project exercise02.circ as structural Verilog: 1 circuit, main circuit main
module main (
  input  A,
  input  B,
  output S
);

  wire NAND1_out, NAND2_out, NAND4_out;

  nand NAND4 (NAND4_out, A, A);
  nand NAND2 (NAND2_out, B, B);
  nand NAND1 (NAND1_out, NAND4_out, NAND4_out);
  nand NAND3 (S, NAND1_out, NAND2_out);
endmodule
