// Logisim project exercise03.circ as structural Verilog: 1 circuit, main circuit main
module main (
  input  B,
  input  A,
  output S
);

  wire NOR1_out, NOR2_out, NOR3_out;

  nor NOR1 (NOR1_out, B, B);
  nor NOR2 (NOR2_out, NOR1_out, NOR1_out);
  nor NOR3 (NOR3_out, A, A);
  nor NOR4 (S, NOR2_out, NOR3_out);
endmodule
