// Logisim project exercise04.circ as structural Verilog: 1 circuit, main circuit main
module main (
  input  A,
  input  B,
  output out_3
);

  wire nand_1_out, nand_2_out;

  nand nand_1 (nand_1_out, A, A);
  nand nand_2 (nand_2_out, nand_1_out, nand_1_out);
  nand nand_3 (out_3, nand_2_out, B);
endmodule
