// Logisim project 1bitcomparatordifference.circ as structural Verilog: 1 circuit, main circuit main
module main (
  input  e,
  input  a,
  input  b,
  output a__b,
  output a_b,
  output a_b_2
);

  wire and_1_out, and_2_out, and_4_out, and_6_out, nor_1_out, not_1_out, not_2_out, not_3_out, not_4_out;

  and and_1 (and_1_out, a, b);
  not not_1 (not_1_out, a);
  not not_2 (not_2_out, b);
  and and_2 (and_2_out, not_1_out, not_2_out);
  nor nor_1 (nor_1_out, and_1_out, and_2_out);
  not not_3 (not_3_out, a);
  not not_4 (not_4_out, b);
  and and_3 (a__b, e, nor_1_out);
  and and_4 (and_4_out, e, b);
  and and_5 (a_b, and_4_out, not_3_out);
  and and_6 (and_6_out, e, a);
  and and_7 (a_b_2, and_6_out, not_4_out);
endmodule
