// Logisim project Guia08.1.circ as structural Verilog: 9 circuits, main circuit main
module main (
  input  X,
  input  Y,
  input  X_2,
  input  Y_2,
  input  X_3,
  input  Y_3,
  input  carry_in,
  output S,
  output S_2,
  output S2,
  output S_3,
  output S_4
);

  wire A_prime_B_2_out, A_prime_B_out, AB_prime_2_out, AB_prime_out, and_1_out, and_2_out, and_3_out,
       and_4_out, and_5_out, and_6_out, and_7_out, and_8_out, and_9_out, and_10_out, and_11_out, and_12_out,
       and_13_out, and_14_out, and_15_out, and_16_out, NOT_carry_in_out, NOT_X_2_out, NOT_X_3_out, NOT_X_out,
       NOT_Y_2_out, NOT_Y_3_out, NOT_Y_out, or_1_out, or_2_out, or_3_out, or_4_out;

  not NOT_X (NOT_X_out, X);
  not NOT_X_2 (NOT_X_2_out, X_3);
  not NOT_Y (NOT_Y_out, Y);
  not NOT_carry_in (NOT_carry_in_out, carry_in);
  not NOT_Y_2 (NOT_Y_2_out, Y_3);
  and AB_prime (AB_prime_out, X, NOT_Y_out);
  and A_prime_B (A_prime_B_out, NOT_X_out, Y);
  and and_1 (and_1_out, NOT_X_2_out, NOT_Y_2_out);
  and and_2 (and_2_out, NOT_X_2_out, Y_3);
  and and_3 (and_3_out, X_3, NOT_Y_2_out);
  and and_4 (and_4_out, X_3, Y_3);
  and and_5 (and_5_out, NOT_X_2_out, Y_3);
  and and_6 (and_6_out, X_3, NOT_Y_2_out);
  and and_7 (and_7_out, X_3, Y_3);
  and and_8 (and_8_out, X_3, Y_3);
  or AB_prime___A_prime_B (S_2, AB_prime_out, A_prime_B_out);
  and and_9 (and_9_out, and_1_out, carry_in);
  and and_10 (and_10_out, and_2_out, NOT_carry_in_out);
  and and_11 (and_11_out, and_3_out, NOT_carry_in_out);
  and and_12 (and_12_out, and_4_out, carry_in);
  and and_13 (and_13_out, and_5_out, carry_in);
  and and_14 (and_14_out, and_6_out, carry_in);
  and and_15 (and_15_out, and_7_out, NOT_carry_in_out);
  and and_16 (and_16_out, and_8_out, carry_in);
  not NOT_X_3 (NOT_X_3_out, X_2);
  or or_1 (or_1_out, and_9_out, and_10_out);
  or or_2 (or_2_out, and_13_out, and_14_out);
  not NOT_Y_3 (NOT_Y_3_out, Y_2);
  or or_3 (or_3_out, or_1_out, and_11_out);
  or or_4 (or_4_out, or_2_out, and_15_out);
  and AB_prime_2 (AB_prime_2_out, X_2, NOT_Y_3_out);
  and A_prime_B_2 (A_prime_B_2_out, NOT_X_3_out, Y_2);
  and AB (S2, X_2, Y_2);
  or or_5 (S_3, or_3_out, and_12_out);
  or or_6 (S_4, or_4_out, and_16_out);
  or AB_prime___A_prime_B_2 (S, AB_prime_2_out, A_prime_B_2_out);

  // Notes on the sheet:
  //   1bit adder
  //   1bit adder w/ carry in and carry out
  //   1bit adder w/ carry out
  //   carry out
endmodule

module _01 (
  input  ci,
  input  A0,
  input  B0,
  input  A1,
  input  B1,
  input  A2,
  input  B2,
  input  A3,
  input  B3,
  input  A4,
  input  B4,
  input  A5,
  input  B5,
  output S0,
  output S1,
  output S2,
  output S3,
  output S4,
  output C4,
  output co
);

  wire fulladder_1_co, fulladder_2_co, fulladder_3_co, fulladder_4_co, fulladder_5_co;

  fulladder_fulladder fulladder_1 (.ci(ci), .a(A0), .b(B0), .s(S0), .co(fulladder_1_co));
  fulladder_fulladder fulladder_2 (.ci(fulladder_1_co), .a(A1), .b(B1), .s(S1), .co(fulladder_2_co));
  fulladder_fulladder fulladder_3 (.ci(fulladder_2_co), .a(A2), .b(B2), .s(S2), .co(fulladder_3_co));
  fulladder_fulladder fulladder_4 (.ci(fulladder_3_co), .a(A3), .b(B3), .s(S3), .co(fulladder_4_co));
  fulladder_fulladder fulladder_5 (.ci(fulladder_4_co), .a(A4), .b(B4), .s(S4), .co(fulladder_5_co));
  fulladder_fulladder fulladder_6 (.ci(fulladder_5_co), .a(A5), .b(B5), .s(C4), .co(co));

  // Notes on the sheet:
  //   adder 5 bits
endmodule

module _02 (
  input  ci,
  input  A0,
  input  B0,
  input  A1,
  input  B1,
  input  A2,
  input  B2,
  input  A3,
  input  B3,
  input  A4,
  input  B4,
  output S0,
  output S1,
  output S2,
  output S3,
  output S4,
  output co
);

  wire fulladder_1_co, fulladder_2_co, fulladder_3_co, fulladder_4_co, xor_1_out, xor_2_out, xor_3_out,
       xor_4_out, xor_5_out;

  xor xor_1 (xor_1_out, B0, ci);
  xor xor_2 (xor_2_out, B1, ci);
  xor xor_3 (xor_3_out, B2, ci);
  xor xor_4 (xor_4_out, B3, ci);
  xor xor_5 (xor_5_out, B4, ci);
  fulladder_fulladder fulladder_1 (.ci(ci), .a(A0), .b(xor_1_out), .s(S0), .co(fulladder_1_co));
  fulladder_fulladder fulladder_2 (.ci(fulladder_1_co), .a(A1), .b(xor_2_out), .s(S1), .co(fulladder_2_co));
  fulladder_fulladder fulladder_3 (.ci(fulladder_2_co), .a(A2), .b(xor_3_out), .s(S2), .co(fulladder_3_co));
  fulladder_fulladder fulladder_4 (.ci(fulladder_3_co), .a(A3), .b(xor_4_out), .s(S3), .co(fulladder_4_co));
  fulladder_fulladder fulladder_5 (.ci(fulladder_4_co), .a(A4), .b(xor_5_out), .s(S4), .co(co));

  // Notes on the sheet:
  //   full-subtractor 5 bits
endmodule

module _03 (
  input  e,
  input  [4:0] a,
  input  [4:0] b,
  output a__b,
  output a_b,
  output a_b_2
);

  wire main_1_a__b, main_1_a_b, main_1_a_b_2, main_2_a__b, main_2_a_b, main_2_a_b_2, main_3_a__b, main_3_a_b,
       main_3_a_b_2, main_4_a__b, main_4_a_b, main_4_a_b_2, main_5_a_b, main_5_a_b_2;

  _1bitcomparator_main main_1 (.a__b(main_1_a__b), .a_b(main_1_a_b), .a_b_2(main_1_a_b_2), .e(e), .a(a[4]), .b(b[4]));
  _1bitcomparator_main main_2 (
    .a__b(main_2_a__b), .a_b(main_2_a_b), .a_b_2(main_2_a_b_2), .e(main_1_a__b), .a(a[3]), .b(b[3]));
  _1bitcomparator_main main_3 (
    .a__b(main_3_a__b), .a_b(main_3_a_b), .a_b_2(main_3_a_b_2), .e(main_2_a__b), .a(a[2]), .b(b[2]));
  _1bitcomparator_main main_4 (
    .a__b(main_4_a__b), .a_b(main_4_a_b), .a_b_2(main_4_a_b_2), .e(main_3_a__b), .a(a[1]), .b(b[1]));
  _1bitcomparator_main main_5 (
    .a__b(a__b), .a_b(main_5_a_b), .a_b_2(main_5_a_b_2), .e(main_4_a__b), .a(a[0]), .b(b[0]));
  or or_1 (a_b, main_5_a_b, main_4_a_b, main_3_a_b, main_2_a_b, main_1_a_b);
  or or_2 (a_b_2, main_5_a_b_2, main_4_a_b_2, main_3_a_b_2, main_2_a_b_2, main_1_a_b_2);

  // Notes on the sheet:
  //   5 bits comparator equals
endmodule

module _04 (
  input  e,
  input  [4:0] a,
  input  [4:0] b,
  output a__b,
  output a_b,
  output a_b_2
);

  wire main_1_a__b, main_1_a_b, main_1_a_b_2, main_2_a__b, main_2_a_b, main_2_a_b_2, main_3_a__b, main_3_a_b,
       main_3_a_b_2, main_4_a__b, main_4_a_b, main_4_a_b_2, main_5_a_b, main_5_a_b_2;

  _1bitcomparatordifference_main main_1 (
    .a__b(main_1_a__b), .a_b(main_1_a_b), .a_b_2(main_1_a_b_2), .e(e), .a(a[4]), .b(b[4]));
  _1bitcomparatordifference_main main_2 (
    .a__b(main_2_a__b), .a_b(main_2_a_b), .a_b_2(main_2_a_b_2), .e(main_1_a__b), .a(a[3]), .b(b[3]));
  _1bitcomparatordifference_main main_3 (
    .a__b(main_3_a__b), .a_b(main_3_a_b), .a_b_2(main_3_a_b_2), .e(main_2_a__b), .a(a[2]), .b(b[2]));
  _1bitcomparatordifference_main main_4 (
    .a__b(main_4_a__b), .a_b(main_4_a_b), .a_b_2(main_4_a_b_2), .e(main_3_a__b), .a(a[1]), .b(b[1]));
  _1bitcomparatordifference_main main_5 (
    .a__b(a__b), .a_b(main_5_a_b), .a_b_2(main_5_a_b_2), .e(main_4_a__b), .a(a[0]), .b(b[0]));
  or or_1 (a_b, main_5_a_b, main_4_a_b, main_3_a_b, main_2_a_b, main_1_a_b);
  or or_2 (a_b_2, main_5_a_b_2, main_4_a_b_2, main_3_a_b_2, main_2_a_b_2, main_1_a_b_2);

  // Notes on the sheet:
  //   5 bits comparator difference
endmodule

module _05 (
  input  [5:0] a,
  input  in_2,
  output s0,
  output s1,
  output s2,
  output s3,
  output co
);

  wire xor_1_out, xor_2_out, xor_3_out, xor_4_out, xor_5_out, xor_6_out;

  xor xor_1 (xor_1_out, a[5], in_2);
  xor xor_2 (xor_2_out, a[4], in_2);
  xor xor_3 (xor_3_out, a[3], in_2);
  xor xor_4 (xor_4_out, a[2], in_2);
  xor xor_5 (xor_5_out, a[1], in_2);
  xor xor_6 (xor_6_out, a[0], in_2);

  // Notes on the sheet:
  //   C2
endmodule

module _06 (
);

  _01 u_01_1 ();  // open: S0, co, ci, A0, B0, A1, B1, A2, B2, A3, B3, A4, B4, S1, S2, S3, S4, C4, A5, B5
endmodule

module fulladder (
  input  ci,
  input  a,
  input  b,
  output s,
  output co
);

  wire halfadder_1_co, halfadder_1_s, halfadder_2_co;

  halfadder_compact_halfadder halfadder_1 (.S(halfadder_1_s), .CO(halfadder_1_co), .X(a), .Y(b));
  halfadder_compact_halfadder halfadder_2 (.S(s), .CO(halfadder_2_co), .X(ci), .Y(halfadder_1_s));
  or or_1 (co, halfadder_2_co, halfadder_1_co);

  // Notes on the sheet:
  //   fulladder
endmodule

module halfadder (
  input  a,
  input  b,
  output S,
  output CO
);

  xor X_Y (S, a, b);
  and XY (CO, a, b);

  // Notes on the sheet:
  //   halfadder
endmodule
