// Logisim project adder.circ as structural Verilog: 1 circuit, main circuit adder
module adder (
  input  X,
  input  Y,
  input  carry_in,
  output S,
  output S_2
);

  wire and_1_out, and_2_out, and_3_out, and_4_out, and_5_out, and_6_out, and_7_out, and_8_out, and_9_out,
       and_10_out, and_11_out, and_12_out, and_13_out, and_14_out, and_15_out, and_16_out, NOT_carry_in_out,
       NOT_X_out, NOT_Y_out, or_1_out, or_2_out, or_3_out, or_4_out;

  not NOT_Y (NOT_Y_out, Y);
  not NOT_X (NOT_X_out, X);
  not NOT_carry_in (NOT_carry_in_out, carry_in);
  and and_1 (and_1_out, NOT_X_out, NOT_Y_out);
  and and_2 (and_2_out, NOT_X_out, Y);
  and and_3 (and_3_out, X, NOT_Y_out);
  and and_4 (and_4_out, X, Y);
  and and_5 (and_5_out, NOT_X_out, Y);
  and and_6 (and_6_out, X, NOT_Y_out);
  and and_7 (and_7_out, X, Y);
  and and_8 (and_8_out, X, Y);
  and and_9 (and_9_out, and_1_out, carry_in);
  and and_10 (and_10_out, and_2_out, NOT_carry_in_out);
  and and_11 (and_11_out, and_3_out, NOT_carry_in_out);
  and and_12 (and_12_out, and_4_out, carry_in);
  and and_13 (and_13_out, and_5_out, carry_in);
  and and_14 (and_14_out, and_6_out, carry_in);
  and and_15 (and_15_out, and_7_out, NOT_carry_in_out);
  and and_16 (and_16_out, and_8_out, carry_in);
  or or_1 (or_1_out, and_9_out, and_10_out);
  or or_2 (or_2_out, and_13_out, and_14_out);
  or or_3 (or_3_out, or_1_out, and_11_out);
  or or_4 (or_4_out, or_2_out, and_15_out);
  or or_5 (S, or_3_out, and_12_out);
  or or_6 (S_2, or_4_out, and_16_out);

  // Notes on the sheet:
  //   1bit adder w/ carry in and carry out
endmodule
