// Logisim project fulladder.circ as structural Verilog: 1 circuit, main circuit fulladder
module fulladder (
  input  ci,
  input  a,
  input  b,
  output s,
  output co
);

  wire halfadder_1_co, halfadder_1_s, halfadder_2_co;

  halfadder halfadder_1 (.S(halfadder_1_s), .CO(halfadder_1_co), .X(a), .Y(b));
  halfadder halfadder_2 (.S(s), .CO(halfadder_2_co), .X(ci), .Y(halfadder_1_s));
  or or_1 (co, halfadder_2_co, halfadder_1_co);
endmodule
