// Logisim project halfadder_compact.circ as structural Verilog: 1 circuit, main circuit halfadder
module halfadder (
  input  X,
  input  Y,
  output S,
  output CO
);

  xor X_Y (S, X, Y);
  and XY (CO, X, Y);
endmodule
