// Logisim project halfsub.circ as structural Verilog: 1 circuit, main circuit main
module main (
  input  ci,
  input  a0,
  input  b0,
  input  a1,
  input  b1,
  input  a2,
  input  b2,
  input  a3,
  input  b3,
  input  a4,
  input  b4,
  output s0,
  output s1,
  output s2,
  output s3,
  output s4,
  output co
);

  wire fulladder_1_co, fulladder_2_co, fulladder_3_co, fulladder_4_co, xor_1_out, xor_2_out, xor_3_out,
       xor_4_out, xor_5_out;

  xor xor_1 (xor_1_out, b0, ci);
  xor xor_2 (xor_2_out, b1, ci);
  xor xor_3 (xor_3_out, b2, ci);
  xor xor_4 (xor_4_out, b3, ci);
  xor xor_5 (xor_5_out, b4, ci);
  fulladder fulladder_1 (.ci(ci), .a(a0), .b(xor_1_out), .s(s0), .co(fulladder_1_co));
  fulladder fulladder_2 (.ci(fulladder_1_co), .a(a1), .b(xor_2_out), .s(s1), .co(fulladder_2_co));
  fulladder fulladder_3 (.ci(fulladder_2_co), .a(a2), .b(xor_3_out), .s(s2), .co(fulladder_3_co));
  fulladder fulladder_4 (.ci(fulladder_3_co), .a(a3), .b(xor_4_out), .s(s3), .co(fulladder_4_co));
  fulladder fulladder_5 (.ci(fulladder_4_co), .a(a4), .b(xor_5_out), .s(s4), .co(co));

  // Notes on the sheet:
  //   full-subtractor
endmodule
