// Logisim project logisim.circ as structural Verilog
module _05 (
  input  a,
  input  b,
  output S
);

  wire nor_1_out, not_1_out, not_2_out, xor_1_out;

  not not_1 (not_1_out, a);
  not not_2 (not_2_out, b);
  nor nor_1 (nor_1_out, not_1_out, not_2_out);
  xor xor_1 (xor_1_out, a, b);
  nand nand_1 (S, nor_1_out, xor_1_out);

  // Notes on the sheet:
  //   NAND (XOR (a, b), NOR (NOT(a),NOT (b)))
endmodule
